// Logisim project PROCESSEUR.circ as structural Verilog: 27 circuits, main circuit simpleBitAdder
module simpleBitAdder (
  input  Retenue_entree,
  input  A,
  input  B,
  output Resultat,
  output Retenue_sortie
);

  wire and_1_out, and_2_out, xor_1_out;

  xor xor_1 (xor_1_out, Retenue_entree, A);
  and and_1 (and_1_out, Retenue_entree, A);
  and and_2 (and_2_out, xor_1_out, B);
  xor xor_2 (Resultat, B, xor_1_out);
  xor xor_3 (Retenue_sortie, and_2_out, and_1_out);
endmodule

module Add (
  input  [7:0] A,
  input  [7:0] B,
  output [7:0] Sortie,
  output Erreur
);

  wire and_1_out, simplebitadder_1_retenue_sortie, simplebitadder_2_retenue_sortie,
       simplebitadder_3_retenue_sortie, simplebitadder_4_retenue_sortie, simplebitadder_5_retenue_sortie,
       simplebitadder_6_retenue_sortie;

  xor xor_1 (Sortie[0], A[0], B[0]);
  and and_1 (and_1_out, A[0], B[0]);
  simpleBitAdder simplebitadder_1 (
    .Retenue_entree(and_1_out), .A(A[1]), .B(B[1]), .Resultat(Sortie[1]),
    .Retenue_sortie(simplebitadder_1_retenue_sortie));
  simpleBitAdder simplebitadder_2 (
    .Retenue_entree(simplebitadder_1_retenue_sortie), .A(A[2]), .B(B[2]), .Resultat(Sortie[2]),
    .Retenue_sortie(simplebitadder_2_retenue_sortie));
  simpleBitAdder simplebitadder_3 (
    .Retenue_entree(simplebitadder_2_retenue_sortie), .A(A[3]), .B(B[3]), .Resultat(Sortie[3]),
    .Retenue_sortie(simplebitadder_3_retenue_sortie));
  simpleBitAdder simplebitadder_4 (
    .Retenue_entree(simplebitadder_3_retenue_sortie), .A(A[4]), .B(B[4]), .Resultat(Sortie[4]),
    .Retenue_sortie(simplebitadder_4_retenue_sortie));
  simpleBitAdder simplebitadder_5 (
    .Retenue_entree(simplebitadder_4_retenue_sortie), .A(A[5]), .B(B[5]), .Resultat(Sortie[5]),
    .Retenue_sortie(simplebitadder_5_retenue_sortie));
  simpleBitAdder simplebitadder_6 (
    .Retenue_entree(simplebitadder_5_retenue_sortie), .A(A[6]), .B(B[6]), .Resultat(Sortie[6]),
    .Retenue_sortie(simplebitadder_6_retenue_sortie));
  simpleBitAdder simplebitadder_7 (
    .Retenue_entree(simplebitadder_6_retenue_sortie), .A(A[7]), .B(B[7]), .Resultat(Sortie[7]),
    .Retenue_sortie(Erreur));
endmodule

module Sub (
  input  [7:0] A,
  input  [7:0] B,
  output [7:0] Sortie,
  output Erreur
);

  wire not_1_out, not_2_out, not_3_out, not_4_out, not_5_out, not_6_out, not_7_out, not_8_out,
       simplebitadder_1_retenue_sortie, simplebitadder_2_retenue_sortie, simplebitadder_3_retenue_sortie,
       simplebitadder_4_retenue_sortie, simplebitadder_5_retenue_sortie, simplebitadder_6_retenue_sortie,
       simplebitadder_7_retenue_sortie, xor_1_out, xor_2_out;

  not not_1 (not_1_out, B[0]);
  not not_2 (not_2_out, B[1]);
  not not_3 (not_3_out, B[2]);
  not not_4 (not_4_out, B[3]);
  not not_5 (not_5_out, B[4]);
  not not_6 (not_6_out, B[5]);
  not not_7 (not_7_out, B[6]);
  not not_8 (not_8_out, B[7]);
  simpleBitAdder simplebitadder_1 (
    .Retenue_entree(A[0]), .A(not_1_out), .B(1'b1), .Resultat(Sortie[0]),
    .Retenue_sortie(simplebitadder_1_retenue_sortie));
  simpleBitAdder simplebitadder_2 (
    .Retenue_entree(simplebitadder_1_retenue_sortie), .A(A[1]), .B(not_2_out), .Resultat(Sortie[1]),
    .Retenue_sortie(simplebitadder_2_retenue_sortie));
  simpleBitAdder simplebitadder_3 (
    .Retenue_entree(simplebitadder_2_retenue_sortie), .A(A[2]), .B(not_3_out), .Resultat(Sortie[2]),
    .Retenue_sortie(simplebitadder_3_retenue_sortie));
  simpleBitAdder simplebitadder_4 (
    .Retenue_entree(simplebitadder_3_retenue_sortie), .A(A[3]), .B(not_4_out), .Resultat(Sortie[3]),
    .Retenue_sortie(simplebitadder_4_retenue_sortie));
  simpleBitAdder simplebitadder_5 (
    .Retenue_entree(simplebitadder_4_retenue_sortie), .A(A[4]), .B(not_5_out), .Resultat(Sortie[4]),
    .Retenue_sortie(simplebitadder_5_retenue_sortie));
  simpleBitAdder simplebitadder_6 (
    .Retenue_entree(simplebitadder_5_retenue_sortie), .A(A[5]), .B(not_6_out), .Resultat(Sortie[5]),
    .Retenue_sortie(simplebitadder_6_retenue_sortie));
  simpleBitAdder simplebitadder_7 (
    .Retenue_entree(simplebitadder_6_retenue_sortie), .A(A[6]), .B(not_7_out), .Resultat(Sortie[6]),
    .Retenue_sortie(simplebitadder_7_retenue_sortie));
  simpleBitAdder simplebitadder_8 (
    .Retenue_entree(simplebitadder_7_retenue_sortie), .A(A[7]), .B(not_8_out), .Resultat(Sortie[7]));  // open: Retenue_sortie
  xor xor_1 (xor_1_out, A[7], B[7]);
  xor xor_2 (xor_2_out, A[7], Sortie[7]);
  and and_1 (Erreur, xor_1_out, xor_2_out);
endmodule

module And8Bit (
  input  [7:0] A,
  input  [7:0] B,
  output [7:0] Sortie
);

  assign Sortie = A & B;  // AND_Gate and_1, 8 bits wide
endmodule

module Or8Bit (
  input  [7:0] A,
  input  [7:0] B,
  output [7:0] Sortie
);

  assign Sortie = A | B;  // OR_Gate or_1, 8 bits wide
endmodule

module Xor8Bit (
  input  [7:0] A,
  input  [7:0] B,
  output [7:0] Sortie
);

  assign Sortie = A ^ B;  // XOR_Gate xor_1, 8 bits wide
endmodule

module Lsl (
  input  [7:0] Entree,
  output [7:0] Sortie
);


  assign Sortie = {Entree[6:0], 1'b0};
endmodule

module Diff (
  input  [7:0] A,
  input  [7:0] B,
  output Sortie
);

  wire and_1_out;
  wire [7:0] not_1_out, xor8bit_1_sortie;

  assign not_1_out = ~B;  // NOT_Gate not_1, 8 bits wide
  Xor8Bit xor8bit_1 (.A(A), .B(not_1_out), .Sortie(xor8bit_1_sortie));
  and and_1 (and_1_out, xor8bit_1_sortie[0], xor8bit_1_sortie[1], xor8bit_1_sortie[2], xor8bit_1_sortie[3], xor8bit_1_sortie[5], xor8bit_1_sortie[6], xor8bit_1_sortie[7], xor8bit_1_sortie[4]);
  not not_2 (Sortie, and_1_out);
endmodule

module ALU (
  input  [7:0] A,
  input  [7:0] B,
  input  [3:0] OP,
  output Erreur,
  output [7:0] Sortie
);

  wire multiplex_operation_1_erreur;
  wire [7:0] multiplex_comparaison_1_sortie, multiplex_logique_1_sortie, multiplex_operation_1_sortie;

  Multiplex_Operation multiplex_operation_1 (
    .A(A), .B(B), .OP(OP[3:2]), .Sortie(multiplex_operation_1_sortie), .Erreur(multiplex_operation_1_erreur));
  Multiplex_Comparaison multiplex_comparaison_1 (.A(A), .B(B), .OP(OP[3:2]), .Sortie(multiplex_comparaison_1_sortie));
  Multiplex_Logique multiplex_logique_1 (.A(A), .B(B), .OP(OP[3:2]), .Sortie(multiplex_logique_1_sortie));
  Multiplexer #(.select(2), .width(8)) multiplexer_1 (
    .in0(multiplex_operation_1_sortie), .in1(multiplex_comparaison_1_sortie),
    .in2(multiplex_logique_1_sortie), .out(Sortie), .sel(OP[1:0]));  // open: in3
  Multiplexer #(.select(2)) multiplexer_2 (
    .in0(multiplex_operation_1_erreur), .in1(1'b0), .in2(1'b0), .in3(1'b0), .out(Erreur), .sel(OP[1:0]));
endmodule

module Multiplex_Operation (
  input  [7:0] A,
  input  [7:0] B,
  input  [1:0] OP,
  output [7:0] Sortie,
  output Erreur
);

  wire add_1_erreur, sub_1_erreur;
  wire [7:0] add_1_sortie, sub_1_sortie;

  Add add_1 (.A(A), .B(B), .Sortie(add_1_sortie), .Erreur(add_1_erreur));
  Sub sub_1 (.A(A), .B(B), .Sortie(sub_1_sortie), .Erreur(sub_1_erreur));
  Multiplexer #(.select(2)) multiplexer_1 (
    .in0(add_1_erreur), .in1(sub_1_erreur), .out(Erreur), .sel(OP));  // open: in2, in3
  Multiplexer #(.select(2), .width(8)) multiplexer_2 (
    .in0(add_1_sortie), .in1(sub_1_sortie), .out(Sortie), .sel(OP));  // open: in2, in3
endmodule

module Multiplex_Comparaison (
  input  [7:0] A,
  input  [7:0] B,
  input  [1:0] OP,
  output [7:0] Sortie
);

  wire comparateur_complet_1_aegb, comparateur_complet_1_ainfb, comparateur_complet_1_asupb, diff_1_sortie;

  Comparateur_Complet comparateur_complet_1 (
    .A(A), .B(B), .ASupB(comparateur_complet_1_asupb), .AEgB(comparateur_complet_1_aegb),
    .AInfB(comparateur_complet_1_ainfb));
  Diff diff_1 (.A(A), .B(B), .Sortie(diff_1_sortie));
  Multiplexer #(.select(2)) multiplexer_1 (
    .in0(comparateur_complet_1_asupb), .in1(comparateur_complet_1_aegb), .in2(comparateur_complet_1_ainfb),
    .in3(diff_1_sortie), .out(Sortie[0]), .sel(OP));

  assign Sortie[7:1] = {7{1'b0}};
endmodule

module Multiplex_Logique (
  input  [7:0] A,
  input  [7:0] B,
  input  [1:0] OP,
  output [7:0] Sortie
);

  wire [7:0] and8bit_1_sortie, or8bit_1_sortie, xor8bit_1_sortie;

  And8Bit and8bit_1 (.A(A), .B(B), .Sortie(and8bit_1_sortie));
  Or8Bit or8bit_1 (.A(A), .B(B), .Sortie(or8bit_1_sortie));
  Xor8Bit xor8bit_1 (.A(A), .B(B), .Sortie(xor8bit_1_sortie));
  Multiplexer #(.select(2), .width(8)) multiplexer_1 (
    .in0(and8bit_1_sortie), .in1(or8bit_1_sortie), .in2(xor8bit_1_sortie), .out(Sortie), .sel(OP));  // open: in3
endmodule

module Registre (
  input  [7:0] Write,
  input  Write_enable,
  output [7:0] Read
);

  wire and_1_out, clock_1_out;

  Clock clock_1 (.out(clock_1_out));
  and and_1 (and_1_out, clock_1_out, Write_enable);
  D_Flip_Flop d_ff_1 (.D(Write[0]), .clk(and_1_out), .Q(Read[0]));  // open: Qn, preset, reset
  D_Flip_Flop d_ff_2 (.D(Write[1]), .clk(and_1_out), .Q(Read[1]));  // open: Qn, preset, reset
  D_Flip_Flop d_ff_3 (.D(Write[2]), .clk(and_1_out), .Q(Read[2]));  // open: Qn, preset, reset
  D_Flip_Flop d_ff_4 (.D(Write[3]), .clk(and_1_out), .Q(Read[3]));  // open: Qn, preset, reset
  D_Flip_Flop d_ff_5 (.D(Write[4]), .clk(and_1_out), .Q(Read[4]));  // open: Qn, preset, reset
  D_Flip_Flop d_ff_6 (.D(Write[5]), .clk(and_1_out), .Q(Read[5]));  // open: Qn, preset, reset
  D_Flip_Flop d_ff_7 (.D(Write[6]), .clk(and_1_out), .Q(Read[6]));  // open: Qn, preset, reset
  D_Flip_Flop d_ff_8 (.D(Write[7]), .clk(and_1_out), .Q(Read[7]));  // open: Qn, preset, reset
endmodule

module Banc_de_registre (
  input  [7:0] Write,
  input  [2:0] slct_C,
  input  [2:0] slct_A,
  input  [2:0] slct_B,
  output [7:0] A,
  output [7:0] B,
  output zero
);

  wire decoder_1_out0, decoder_1_out1, decoder_1_out2, decoder_1_out3, decoder_1_out4, decoder_1_out5,
       decoder_1_out6, decoder_1_out7;
  wire [7:0] registre_1_read, registre_2_read, registre_3_read, registre_4_read, registre_5_read,
       registre_6_read, registre_7_read;

  Decoder #(.select(3)) decoder_1 (
    .out0(decoder_1_out0), .out1(decoder_1_out1), .out2(decoder_1_out2), .out3(decoder_1_out3),
    .out4(decoder_1_out4), .out5(decoder_1_out5), .out6(decoder_1_out6), .out7(decoder_1_out7), .sel(slct_C));  // open: en
  Registre registre_1 (.Write(Write), .Write_enable(decoder_1_out0), .Read(registre_1_read));
  Registre registre_2 (.Write(Write), .Write_enable(decoder_1_out1), .Read(registre_2_read));
  Registre registre_3 (.Write(Write), .Write_enable(decoder_1_out2), .Read(registre_3_read));
  Registre registre_4 (.Write(Write), .Write_enable(decoder_1_out3), .Read(registre_4_read));
  Registre registre_5 (.Write(Write), .Write_enable(decoder_1_out4), .Read(registre_5_read));
  Registre registre_6 (.Write(Write), .Write_enable(decoder_1_out5), .Read(registre_6_read));
  Registre registre_7 (.Write(Write), .Write_enable(decoder_1_out6), .Read(registre_7_read));
  Registre_1Bit registre_1bit_1 (.Write_enable(decoder_1_out7), .Write(Write[0]), .Read(zero));
  Multiplexer #(.select(3), .width(8)) multiplexer_1 (
    .in0(registre_1_read), .in1(registre_2_read), .in2(registre_3_read), .in3(registre_4_read),
    .in4(registre_5_read), .in5(registre_6_read), .in6(registre_7_read), .out(A), .sel(slct_B));  // open: in7
  Multiplexer #(.select(3), .width(8)) multiplexer_2 (
    .in0(registre_1_read), .in1(registre_2_read), .in2(registre_3_read), .in3(registre_4_read),
    .in4(registre_5_read), .in5(registre_6_read), .in6(registre_7_read), .in7({{7{1'b0}}, zero}), .out(B),
    .sel(slct_A));
endmodule

module Registre_1Bit (
  input  Write_enable,
  input  Write,
  output Read
);

  wire and_1_out, clock_1_out;

  Clock clock_1 (.out(clock_1_out));
  and and_1 (and_1_out, clock_1_out, Write_enable);
  D_Flip_Flop d_ff_1 (.D(Write), .clk(and_1_out), .Q(Read));  // open: Qn, preset, reset
endmodule

module LSR (
  input  [7:0] A,
  output [7:0] Sortie
);


  assign Sortie = {1'b0, A[7:1]};
endmodule

module ASR (
  input  [7:0] A,
  output [7:0] Sortie
);


  assign Sortie = {{2{A[7]}}, A[6:1]};
endmodule

module ROL_circuit (
  input  [7:0] A,
  output [7:0] Sortie
);


  assign Sortie = {A[6:0], A[7]};
endmodule

module ROR_circuit (
  input  [7:0] A,
  output [7:0] Sortie
);


  assign Sortie = {A[0], A[7:1]};
endmodule

module Mulitplex_Dec_et_Rot (
  input  [7:0] A,
  input  [2:0] OP,
  output [7:0] out_3
);

  wire [7:0] asr_1_sortie, lsl_1_sortie, lsr_1_sortie, rol_circuit_1_sortie, ror_circuit_1_sortie;

  Lsl lsl_1 (.Entree(A), .Sortie(lsl_1_sortie));
  LSR lsr_1 (.A(A), .Sortie(lsr_1_sortie));
  ASR asr_1 (.A(A), .Sortie(asr_1_sortie));
  ROL_circuit rol_circuit_1 (.A(A), .Sortie(rol_circuit_1_sortie));
  ROR_circuit ror_circuit_1 (.A(A), .Sortie(ror_circuit_1_sortie));
  Multiplexer #(.select(3), .width(8)) multiplexer_1 (
    .in0(lsl_1_sortie), .in1(lsr_1_sortie), .in2(asr_1_sortie), .in3(rol_circuit_1_sortie),
    .in4(ror_circuit_1_sortie), .out(out_3), .sel(OP));  // open: in5, in6, in7
endmodule

module simpleBitComparateur (
  input  A,
  input  B,
  input  I_ASupB,
  input  I_AEgB,
  input  I_AInfB,
  output O_ASupB,
  output O_AEgB,
  output O_AInfB
);

  wire and_1_out, and_2_out, and_3_out, and_4_out, not_1_out, not_2_out, not_3_out, xor_1_out;

  not not_1 (not_1_out, B);
  not not_2 (not_2_out, A);
  and and_1 (and_1_out, A, not_1_out);
  xor xor_1 (xor_1_out, A, B);
  not not_3 (not_3_out, xor_1_out);
  and and_2 (and_2_out, not_2_out, B);
  and and_3 (and_3_out, I_ASupB, not_3_out);
  and and_4 (and_4_out, not_3_out, I_AInfB);
  or or_1 (O_ASupB, and_1_out, and_3_out);
  and and_5 (O_AEgB, not_3_out, I_AEgB);
  or or_2 (O_AInfB, and_4_out, and_2_out);
endmodule

module Comparateur_Complet (
  input  [7:0] A,
  input  [7:0] B,
  output ASupB,
  output AEgB,
  output AInfB
);

  wire and_1_out, and_2_out, not_1_out, not_2_out, not_3_out, not_4_out, not_5_out,
       simplebitcomparateur_1_o_aegb, simplebitcomparateur_1_o_ainfb, simplebitcomparateur_1_o_asupb,
       simplebitcomparateur_2_o_aegb, simplebitcomparateur_2_o_ainfb, simplebitcomparateur_2_o_asupb,
       simplebitcomparateur_3_o_aegb, simplebitcomparateur_3_o_ainfb, simplebitcomparateur_3_o_asupb,
       simplebitcomparateur_4_o_aegb, simplebitcomparateur_4_o_ainfb, simplebitcomparateur_4_o_asupb,
       simplebitcomparateur_5_o_aegb, simplebitcomparateur_5_o_ainfb, simplebitcomparateur_5_o_asupb,
       simplebitcomparateur_6_o_aegb, simplebitcomparateur_6_o_ainfb, simplebitcomparateur_6_o_asupb,
       xor_1_out;

  not not_1 (not_1_out, A[7]);
  not not_2 (not_2_out, B[7]);
  not not_3 (not_3_out, B[0]);
  not not_4 (not_4_out, A[0]);
  and and_1 (and_1_out, not_3_out, A[0]);
  xor xor_1 (xor_1_out, B[0], A[0]);
  and and_2 (and_2_out, B[0], not_4_out);
  not not_5 (not_5_out, xor_1_out);
  simpleBitComparateur simplebitcomparateur_1 (
    .A(A[1]), .B(B[1]), .I_ASupB(and_1_out), .I_AEgB(not_5_out), .I_AInfB(and_2_out),
    .O_ASupB(simplebitcomparateur_1_o_asupb), .O_AEgB(simplebitcomparateur_1_o_aegb),
    .O_AInfB(simplebitcomparateur_1_o_ainfb));
  simpleBitComparateur simplebitcomparateur_2 (
    .A(A[2]), .B(B[2]), .I_ASupB(simplebitcomparateur_1_o_asupb), .I_AEgB(simplebitcomparateur_1_o_aegb),
    .I_AInfB(simplebitcomparateur_1_o_ainfb), .O_ASupB(simplebitcomparateur_2_o_asupb),
    .O_AEgB(simplebitcomparateur_2_o_aegb), .O_AInfB(simplebitcomparateur_2_o_ainfb));
  simpleBitComparateur simplebitcomparateur_3 (
    .A(A[3]), .B(B[3]), .I_ASupB(simplebitcomparateur_2_o_asupb), .I_AEgB(simplebitcomparateur_2_o_aegb),
    .I_AInfB(simplebitcomparateur_2_o_ainfb), .O_ASupB(simplebitcomparateur_3_o_asupb),
    .O_AEgB(simplebitcomparateur_3_o_aegb), .O_AInfB(simplebitcomparateur_3_o_ainfb));
  simpleBitComparateur simplebitcomparateur_4 (
    .A(A[4]), .B(B[4]), .I_ASupB(simplebitcomparateur_3_o_asupb), .I_AEgB(simplebitcomparateur_3_o_aegb),
    .I_AInfB(simplebitcomparateur_3_o_ainfb), .O_ASupB(simplebitcomparateur_4_o_asupb),
    .O_AEgB(simplebitcomparateur_4_o_aegb), .O_AInfB(simplebitcomparateur_4_o_ainfb));
  simpleBitComparateur simplebitcomparateur_5 (
    .A(A[5]), .B(B[5]), .I_ASupB(simplebitcomparateur_4_o_asupb), .I_AEgB(simplebitcomparateur_4_o_aegb),
    .I_AInfB(simplebitcomparateur_4_o_ainfb), .O_ASupB(simplebitcomparateur_5_o_asupb),
    .O_AEgB(simplebitcomparateur_5_o_aegb), .O_AInfB(simplebitcomparateur_5_o_ainfb));
  simpleBitComparateur simplebitcomparateur_6 (
    .A(A[6]), .B(B[6]), .I_ASupB(simplebitcomparateur_5_o_asupb), .I_AEgB(simplebitcomparateur_5_o_aegb),
    .I_AInfB(simplebitcomparateur_5_o_ainfb), .O_ASupB(simplebitcomparateur_6_o_asupb),
    .O_AEgB(simplebitcomparateur_6_o_aegb), .O_AInfB(simplebitcomparateur_6_o_ainfb));
  simpleBitComparateur simplebitcomparateur_7 (
    .A(not_1_out), .B(not_2_out), .I_ASupB(simplebitcomparateur_6_o_asupb),
    .I_AEgB(simplebitcomparateur_6_o_aegb), .I_AInfB(simplebitcomparateur_6_o_ainfb), .O_ASupB(ASupB),
    .O_AEgB(AEgB), .O_AInfB(AInfB));
endmodule

module Decodeur (
  input  [23:0] in_1,
  output [3:0] slct_OP,
  output [2:0] slct_a,
  output [2:0] slct_B,
  output [2:0] slct_C
);

  Operation_decodeur operation_decodeur_1 (.Code_Decodeur(in_1[7:0]), .Code_ALU(slct_OP));
  Registre_24Bit registre_24bit_1 (.Write(in_1), .Write_enable(1'b1));  // open: Read

  assign slct_a = in_1[10:8];
  assign slct_B = in_1[14:12];
  assign slct_C = in_1[22:20];
endmodule

module circuit_test (
  input  [23:0] in_1
);

  wire banc_de_registre_1_p1;
  wire [2:0] decodeur_1_slct_a, decodeur_1_slct_b, decodeur_1_slct_c;
  wire [3:0] decodeur_1_slct_op;

  Decodeur decodeur_1 (
    .in_1(in_1), .slct_OP(decodeur_1_slct_op), .slct_a(decodeur_1_slct_a), .slct_B(decodeur_1_slct_b),
    .slct_C(decodeur_1_slct_c));
  // Banc_de_registre banc_de_registre_1: pin names not known; wires that end beside it: banc_de_registre_1_p1, decodeur_1_slct_op, decodeur_1_slct_a, decodeur_1_slct_b, decodeur_1_slct_c, banc_de_registre_1_p1
endmodule

module main (
  input  [2:0] in_1,
  input  [2:0] in_2,
  input  [3:0] in_3,
  input  [2:0] in_4,
  output [7:0] out_5,
  output [7:0] out_6
);

  wire [7:0] banc_de_registre_1_b;

  Banc_de_registre banc_de_registre_1 (
    .Write(out_6), .slct_C(in_1), .slct_A(in_2), .slct_B(in_4), .A(out_5), .B(banc_de_registre_1_b));  // open: zero
  ALU alu_1 (.A(out_5), .B(banc_de_registre_1_b), .OP(in_3), .Sortie(out_6));  // open: Erreur
endmodule

module Operation_decodeur (
  input  [7:0] Code_Decodeur,
  output [3:0] Code_ALU
);

  wire and_1_out, and_2_out, and_3_out, and_4_out, and_5_out, and_6_out, and_7_out, and_8_out, and_9_out,
       and_10_out, and_11_out, not_1_out, not_2_out, not_3_out, not_4_out, not_5_out, not_6_out, not_7_out,
       not_8_out;

  not not_1 (not_1_out, Code_Decodeur[7]);
  not not_2 (not_2_out, Code_Decodeur[6]);
  not not_3 (not_3_out, Code_Decodeur[5]);
  not not_4 (not_4_out, Code_Decodeur[4]);
  not not_5 (not_5_out, Code_Decodeur[3]);
  not not_6 (not_6_out, Code_Decodeur[2]);
  not not_7 (not_7_out, Code_Decodeur[1]);
  not not_8 (not_8_out, Code_Decodeur[0]);
  and and_1 (and_1_out, not_1_out, not_2_out, not_3_out, Code_Decodeur[4], not_5_out, not_6_out, not_7_out);
  and and_2 (and_2_out, not_1_out, not_2_out, not_3_out, Code_Decodeur[4], not_5_out, not_6_out, not_8_out);
  and and_3 (and_3_out, not_1_out, not_2_out, not_3_out, not_4_out, not_5_out, not_6_out, Code_Decodeur[0]);
  and and_4 (and_4_out, not_1_out, not_2_out, not_3_out, not_4_out, not_5_out, not_7_out, Code_Decodeur[0]);
  and and_5 (and_5_out, not_1_out, not_2_out, not_3_out, not_4_out, not_5_out, Code_Decodeur[2], Code_Decodeur[1], not_8_out);
  and and_6 (and_6_out, not_1_out, not_2_out, not_3_out, not_4_out, not_5_out, not_6_out, not_7_out, Code_Decodeur[0]);
  and and_7 (and_7_out, not_1_out, not_2_out, not_3_out, Code_Decodeur[4], not_5_out, not_6_out, Code_Decodeur[1], not_8_out);
  and and_8 (and_8_out, not_1_out, not_2_out, not_3_out, not_4_out, not_5_out, Code_Decodeur[2], Code_Decodeur[1], not_8_out);
  and and_9 (and_9_out, not_1_out, not_2_out, not_3_out, Code_Decodeur[4], not_6_out, not_7_out, Code_Decodeur[0]);
  and and_10 (and_10_out, not_1_out, not_2_out, not_3_out, not_4_out, not_5_out, not_6_out, Code_Decodeur[1], Code_Decodeur[0]);
  and and_11 (and_11_out, not_1_out, not_2_out, not_3_out, not_4_out, not_5_out, Code_Decodeur[2], Code_Decodeur[1], not_8_out);
  or or_1 (Code_ALU[3], and_1_out, and_2_out);
  or or_2 (Code_ALU[2], and_3_out, and_4_out, and_5_out);
  or or_3 (Code_ALU[1], and_6_out, and_7_out, and_8_out);
  or or_4 (Code_ALU[0], and_9_out, and_10_out, and_11_out);
endmodule

module Registre_24Bit (
  input  [23:0] Write,
  input  Write_enable,
  output [23:0] Read
);

  Registre registre_1 (.Write(Write[7:0]), .Write_enable(Write_enable), .Read(Read[7:0]));
  Registre registre_2 (.Write(Write[15:8]), .Write_enable(Write_enable), .Read(Read[15:8]));
  Registre registre_3 (.Write(Write[23:16]), .Write_enable(Write_enable), .Read(Read[23:16]));
endmodule
